// Logisim project lab8-1.circ as structural Verilog: 2 circuits, main circuit main
module main (
  input  Pc,
  input  Inc,
  input  Amux,
  input  Mar,
  input  Mst,
  input  Ir,
  input  Dmux,
  input  Acc,
  input  Out,
  input  Sub,
  output [7:0] out_11
);

  wire Add_out, and_1_out, clock_1_out, Clr_out, decoder_1_out0, decoder_1_out1, decoder_1_out2,
       decoder_1_out3, Halt_out, Jaz_out, Jmp_out, Lda_out, Out_2_out, Sta_out, Sub_out;
  wire [1:0] counter_1_q;
  wire [3:0] Ir_q, Mar_q, multiplexer_1_out, not_1_out, Pc_q;
  wire [7:0] Acc_q, adder_1_out, multiplexer_2_out, ram_1_data, xor_1_out;
  wire [7:4] Ir_q_2;

  Clock clock_1 (.out(clock_1_out));
  and and_1 (and_1_out, clock_1_out, Halt_out);
  Button Clr (.out(Clr_out));
  Counter #(.width(4), .max('hf)) u_Pc (
    .load(Pc), .D(Ir_q), .count(Inc), .Q(Pc_q), .clk(and_1_out), .clr(Clr_out));  // open: carry
  Multiplexer #(.width(4), .enable("false")) multiplexer_1 (
    .in0(Pc_q), .in1(Ir_q), .out(multiplexer_1_out), .sel(Amux));
  Counter #(.width(2), .max('h3)) counter_1 (
    .Q(counter_1_q), .clk(and_1_out), .clr(Clr_out));  // open: load, D, count, carry
  Register #(.width(4)) u_Mar (.D(multiplexer_1_out), .en(Mar), .Q(Mar_q), .clk(and_1_out));  // open: clr
  Decoder #(.select(2), .enable("false")) decoder_1 (
    .out0(decoder_1_out0), .out1(decoder_1_out1), .out2(decoder_1_out2), .out3(decoder_1_out3),
    .sel(counter_1_q));
  Control_Logic_Component control_logic_component_1 (
    .Pc(Pc), .Inc(Inc), .Amux(Amux), .Mar(Mar), .Mst(Mst), .Ir(Ir), .Dmux(Dmux), .Acc(Acc), .Out_2(Out),
    .Sub_2(Sub), .t1(decoder_1_out0), .t2(decoder_1_out1), .t3(decoder_1_out2), .t4(decoder_1_out3),
    .Out(Out_2_out), .Jaz(Jaz_out), .Jmp(Jmp_out), .Sta(Sta_out), .Sub(Sub_out), .Add(Add_out), .Lda(Lda_out));
  RAM #(.addrWidth(4), .bus("separate")) ram_1 (
    .addr(Mar_q), .din(Acc_q), .data(ram_1_data), .str(Mst), .clk(and_1_out));  // open: sel, ld, clr
  Multiplexer #(.width(8), .enable("false")) multiplexer_2 (
    .in0(adder_1_out), .in1(ram_1_data), .out(multiplexer_2_out), .sel(Dmux));
  Register u_Ir (.D(ram_1_data), .en(Ir), .Q({Ir_q_2, Ir_q}), .clk(and_1_out), .clr(Clr_out));
  Register u_Acc (.D(multiplexer_2_out), .en(Acc), .Q(Acc_q), .clk(and_1_out));  // open: clr
  Register u_Out (.D(Acc_q), .en(Out), .Q(out_11), .clk(and_1_out));  // open: clr
  assign xor_1_out = ram_1_data ^ {8{Sub}};  // XOR_Gate xor_1, 8 bits wide
  and Lda (Lda_out, not_1_out[3], not_1_out[2], not_1_out[1], not_1_out[0]);
  and Add (Add_out, not_1_out[3], not_1_out[2], not_1_out[1], Ir_q_2[4]);
  and u_Sub (Sub_out, not_1_out[3], not_1_out[2], Ir_q_2[5], not_1_out[0]);
  and Sta (Sta_out, not_1_out[3], not_1_out[2], Ir_q_2[5], Ir_q_2[4]);
  and Jmp (Jmp_out, not_1_out[3], Ir_q_2[6], not_1_out[1], not_1_out[0]);
  and Jaz (Jaz_out, not_1_out[3], Ir_q_2[6], not_1_out[1], Ir_q_2[4]);
  and Out_2 (Out_2_out, Ir_q_2[7], Ir_q_2[6], Ir_q_2[5], not_1_out[0]);
  nand Halt (Halt_out, Ir_q_2[7], Ir_q_2[6], Ir_q_2[5], Ir_q_2[4]);
  Adder adder_1 (.a(Acc_q), .b(xor_1_out), .out(adder_1_out), .cin(Sub));  // open: cout
  assign not_1_out = ~Ir_q_2;  // NOT_Gate not_1, 4 bits wide
endmodule

// Control Logic
module Control_Logic_Component (
  input  t1,
  input  t2,
  input  t3,
  input  t4,
  input  Out,
  input  Jaz,
  input  Jmp,
  input  Sta,
  input  Sub,
  input  Add,
  input  Lda,
  output Pc,
  output Inc,
  output Amux,
  output Mar,
  output Mst,
  output Ir,
  output Dmux,
  output Acc,
  output Out_2,
  output Sub_2
);
endmodule
